# Fritzing sketch QNAP-serial (saved by Fritzing 1.0.1rc)

parts:
  USBTTL1 = USB TTL Serial Cable
  JP1 = Header 4 [package=jst-4-pth]

nets:
  N1: USBTTL1.RX, JP1.1
  N2: USBTTL1.TX, JP1.3
  N3: USBTTL1.GND, JP1.4

notes:
  1
  4
  Green - TX
  White - RX
  Black - GND
  Red - 5V
